# Fritzing sketch Praticando_FreeRTOS (saved by Fritzing 0.9.3b)
breadboards: 1

parts:
  Componente1 = Adafruit HUZZAH32 ESP32 Feather [part_number="Adafruit #3405"]
  Componente2 = LCD1602-I2C
  U1 = POT [package=pot_alpha_rv16af-20]
  S1 = Pushbutton [package="[THT]"]
  R1 = Resistor [tolerance=±5% resistance=150 package="0402 [SMD]"]
  LED1 = smd LED [color="Blue (470nm)" package="0603 [SMD]"]

nets:
  N1: Componente1.IO21, S1.Pin_3, S1.Pin_4
  N2: Componente1.A5_IO4, U1.S
  GND: Componente1.GND, Componente2.GND, U1.E, S1.Pin_1, S1.Pin_2, R1.Pin_0
  N3: Componente1.3.3V, U1.A
  N4: Componente1.VBUS, Componente2.VCC
  N5: Componente1.IO14_A6, LED1.anode
  N6: Componente1.SCL, Componente2.SCL
  N7: Componente1.SDA, Componente2.SDA
  N8: R1.Pin_1, LED1.cathode

custom parts:
  LCD1602-I2C: A standard character display, usually with 2x16 characters. Comes in many colors with LCM1602 IIC attached.
